// Logisim project Register_Riscrev.circ as structural Verilog
module Register_1_0_30f70db8 (
  input  [2:0] Write_Register,
  input  [2:0] in_2,
  input  [2:0] Read_Register_2,
  input  in_4,
  input  [7:0] in_5,
  output [7:0] out_6,
  output [7:0] out_7
);

  wire and_1_out, and_2_out, and_3_out, and_4_out, and_5_out, and_6_out, and_7_out, and_8_out, clock_1_out,
       decoder_1_out0, decoder_1_out1, decoder_1_out2, decoder_1_out3, decoder_1_out4, decoder_1_out5,
       decoder_1_out6, decoder_1_out7;
  wire [7:0] register_1_q, register_2_q, register_3_q, register_4_q, register_5_q, register_6_q,
       register_7_q, register_8_q;

  Decoder #(.select(3)) decoder_1 (
    .out0(decoder_1_out0), .out1(decoder_1_out1), .out2(decoder_1_out2), .out3(decoder_1_out3),
    .out4(decoder_1_out4), .out5(decoder_1_out5), .out6(decoder_1_out6), .out7(decoder_1_out7),
    .sel(Write_Register));  // open: en
  and and_1 (and_1_out, decoder_1_out0, in_4);
  and and_2 (and_2_out, decoder_1_out1, in_4);
  and and_3 (and_3_out, decoder_1_out2, in_4);
  and and_4 (and_4_out, decoder_1_out3, in_4);
  and and_5 (and_5_out, decoder_1_out4, in_4);
  and and_6 (and_6_out, decoder_1_out5, in_4);
  and and_7 (and_7_out, decoder_1_out6, in_4);
  and and_8 (and_8_out, decoder_1_out7, in_4);
  Clock clock_1 (.out(clock_1_out));
  Register register_1 (.D(in_5), .en(and_1_out), .clk(clock_1_out), .Q(register_1_q));  // open: clr
  Register register_2 (.D(in_5), .en(and_2_out), .clk(clock_1_out), .Q(register_2_q));  // open: clr
  Register register_3 (.D(in_5), .en(and_3_out), .clk(clock_1_out), .Q(register_3_q));  // open: clr
  Register register_4 (.D(in_5), .en(and_4_out), .clk(clock_1_out), .Q(register_4_q));  // open: clr
  Register register_5 (.D(in_5), .en(and_5_out), .clk(clock_1_out), .Q(register_5_q));  // open: clr
  Register register_6 (.D(in_5), .en(and_6_out), .clk(clock_1_out), .Q(register_6_q));  // open: clr
  Register register_7 (.D(in_5), .en(and_7_out), .clk(clock_1_out), .Q(register_7_q));  // open: clr
  Register register_8 (.D(in_5), .en(and_8_out), .clk(clock_1_out), .Q(register_8_q));  // open: clr
  Multiplexer #(.select(3), .width(8)) multiplexer_1 (
    .in0(register_1_q), .in1(register_2_q), .in2(register_3_q), .in3(register_4_q), .in4(register_5_q),
    .in5(register_6_q), .in6(register_7_q), .in7(register_8_q), .out(out_6), .sel(in_2));
  Multiplexer #(.select(3), .width(8)) multiplexer_2 (
    .in0(register_1_q), .in1(register_2_q), .in2(register_3_q), .in3(register_4_q), .in4(register_5_q),
    .in5(register_6_q), .in6(register_7_q), .in7(register_8_q), .out(out_7), .sel(Read_Register_2));

  // Notes on the sheet:
  //   Write Data
  //   8*8 Register file-Dual Read,SingleWrite
  //   Read Register 1
endmodule
